// Logisim project full subtractor.circ as structural Verilog: 1 circuit, main circuit main
module main (
  input  A,
  input  B,
  input  Bin,
  output D,
  output Bout
);

  wire and_1_out, and_2_out, not_1_out, not_2_out, xor_1_out;

  not not_1 (not_1_out, A);
  xor xor_1 (xor_1_out, A, B);
  not not_2 (not_2_out, xor_1_out);
  xor xor_2 (D, xor_1_out, Bin);
  and and_1 (and_1_out, B, not_1_out);
  and and_2 (and_2_out, not_2_out, Bin);
  or or_1 (Bout, and_2_out, and_1_out);

  // Notes on the sheet:
  //   A XOR B
  //   A'B
  //   Full Subtractor
  //   (A XOR B)' AND Bin
  //   A XOR B XOR Bin
  //   A'B OR ((A XOR B)' AND Bin)
endmodule
